# Fritzing sketch JunkersRegelung (saved by Fritzing 0.9.1b)
circuit board: 6.88566cm x 5.36311cm
breadboards: 1

parts:
  IC2 = IC, DIP package, 8 pins [chip_label=IC part_number=LM358]
  C1 = Ceramic Capacitor [capacitance=1µF package="100 mil [THT, multilayer]"]
  IC1 = IC, DIP package, 8 pins [chip_label=IC part_number="LTC1257 CN8"]
  R1 = Resistor [tolerance=±1% resistance=10 package=THT]
  R2 = Resistor [tolerance=±1% resistance=100 package=THT]
  C2 = Ceramic Capacitor [capacitance=100nF package="100 mil [THT, multilayer]"]
  R3 = Resistor [tolerance=±1% resistance=110k package=THT]
  R4 = Resistor [tolerance=±1% resistance=10k package=THT]
  J1 = screw terminal, 3 pins
  C3 = Electrolytic Capacitor [capacitance=22µF voltage=35V package="100 mil [THT, electrolytic]"]
  D1 = Schottky Diode [part_number=11DQ06 package="300 mil [THT]"]
  C4 = Electrolytic Capacitor [capacitance=220µF package="100 mil [THT, electrolytic]"]
  Bauteil1 = Arduino Uno (Rev3)
  L1 = Inductor [inductance=330µH package="400 mil [THT]"]
  IC3 = IC, DIP package, 8 pins [chip_label=IC part_number=LM2574N-12]
  JP1 = Jumper [package=sj_2s]
  Q1 = PNP-Transistor [part_number=DS18B20 package="TO92 [THT]"]
  R5 = Resistor [tolerance=±5% resistance=4.7k package=THT]

nets:
  N1: IC2.pin1, R3.Pin_1, J1.pin2
  N2: IC2.pin2, R3.Pin_0, R4.Pin_1
  N3: IC2.pin3, R2.Pin_1, C2.1
  GND: IC2.pin4, IC1.pin5, R1.Pin_0, C2.0, R4.Pin_0, J1.pin3, C3.-, D1.anode, C4.-, Bauteil1.GND, IC3.pin2, IC3.pin3, IC3.pin4, Q1.B
  N4: IC2.pin8, J1.pin1, C3.+, IC3.pin5, JP1.1, JP1.2
  N5: C1.0, R1.Pin_1
  N6: C1.1, IC1.pin6
  N7: IC1.pin1, Bauteil1.D3_PWM
  N8: IC1.pin2, Bauteil1.D4
  N9: IC1.pin3, Bauteil1.D5_PWM
  N10: IC1.pin7, R2.Pin_0
  5V: IC1.pin8, Bauteil1.5V, Q1.C, R5.Pin_0
  N11: D1.cathode, L1.pin_0, IC3.pin7
  N12: C4.+, Bauteil1.VIN, L1.pin_1, IC3.pin1
  N13: Bauteil1.D8, Q1.E, R5.Pin_1

notes:
  VCC
  GND
  Str
